# Fritzing sketch mini Project 2 (saved by Fritzing 0.9.3b)
breadboards: 1

parts:
  S2 = Momentary Switch [package=ksa_sealed_tac_switch]
  U2 = NodeMCU V1.0
  R3 = Resistor [tolerance=±10% resistance=330 package=THT]
  LED4 = LED - 5mm [color="Red (633nm)" package="5 mm [THT]"]
  LED5 = LED - 5mm [color="Yellow (585nm)" package="5 mm [THT]"]
  LED6 = LED - 5mm [color="Green (555nm)" package="5 mm [THT]"]
  R4 = Resistor [tolerance=±5% resistance=220 package=THT]
  DHT2 = DHT11 Humitidy and Temperature Sensor

nets:
  N1: S2.1, U2.D0, R4.Pin_0
  N2: S2.4, U2.Vin
  N3: U2.D1, LED6.anode
  N4: U2.D2, LED5.anode
  N5: U2.D3, LED4.anode
  N6: U2.D4, DHT2.DATA
  3V3: U2.3V3, DHT2.VDD
  GND: U2.GND, R3.Pin_0, R4.Pin_1, DHT2.GND
  N7: R3.Pin_1, LED4.cathode, LED5.cathode, LED6.cathode

custom parts:
  NodeMCU V1.0: ESP8266 based NodeMCU
  DHT11 Humitidy and Temperature Sensor: DHT11 Humidity and Temperature Sensor
